// Logisim project logisim_diagram (1).circ as structural Verilog: 10 circuits, main circuit Junction
module Main (
);

  wire _0_out, _1_out, _2_out, _3_out, _4_out, _5_out, _6_out, and_1_out, and_2_out, and_3_out, and_4_out,
       and_5_out, and_6_out, and_7_out, block_1_availability_of_slot_in_block, block_1_input_for_button7,
       block_1_out_4, block_1_out_5, block_1_out_6, block_2_availability_of_slot_in_block,
       block_2_input_for_button7, block_2_out_4, block_2_out_5, block_2_out_6,
       block_3_availability_of_slot_in_block, block_3_input_for_button7, block_3_out_4, block_3_out_5,
       block_3_out_6, block_4_availability_of_slot_in_block, block_4_input_for_button7, block_4_out_4,
       block_4_out_5, block_4_out_6, block_5_availability_of_slot_in_block, block_5_input_for_button7,
       block_5_out_4, block_5_out_5, block_5_out_6, block_6_availability_of_slot_in_block, block_6_out_4,
       block_6_out_5, block_6_out_6, block_7_availability_of_slot_in_block, block_7_input_for_button7,
       block_7_out_4, block_7_out_5, block_7_out_6, block_8_availability_of_slot_in_block,
       block_8_input_for_button7, block_8_out_4, block_8_out_5, block_8_out_6, clock_1_out, clock_2_out,
       clock_3_out, clock_4_out, clock_5_out, clock_6_out, clock_7_out, clock_8_out, clock_9_out,
       clock_10_out, clock_11_out, clock_12_out, clock_13_out, clock_14_out, clock_15_out, clock_16_out,
       clock_17_out, clock_18_out, clock_19_out, clock_20_out, clock_21_out, clock_22_out, clock_23_out,
       clock_24_out, junction1_1_nl, junction2_1_el, junction2_1_nl, junction3_1_el, junction3_1_sl,
       junction4_1_wl, or_1_out;
  wire [1:0] junction1_1_output_direction, junction2_1_output_direction;
  wire [2:0] Block_Chooser_block_number;
  wire [7:0] junction1_1_newpath2, junction2_1_newpath3, junction2_1_newpath4, Path_Generator_out_2;

  LED led_1 (.in(block_3_availability_of_slot_in_block));
  Button _0 (.out(_0_out));
  and and_1 (and_1_out, block_3_availability_of_slot_in_block, _0_out);
  LED led_2 (.in(block_1_availability_of_slot_in_block));
  LED led_3 (.in(block_4_availability_of_slot_in_block));
  Button _1 (.out(_1_out));
  Button _2 (.out(_2_out));
  and and_2 (and_2_out, block_7_availability_of_slot_in_block, _3_out);
  and and_3 (and_3_out, block_4_availability_of_slot_in_block, _2_out);
  and and_4 (and_4_out, block_1_availability_of_slot_in_block, _1_out);
  LED led_4 (.in(block_5_availability_of_slot_in_block));
  LED led_5 (.in(block_7_availability_of_slot_in_block));
  LED led_6 (.in(block_2_availability_of_slot_in_block));
  Button _5 (.out(_5_out));
  Button _4 (.out(_4_out));
  Button _3 (.out(_3_out));
  and and_5 (and_5_out, block_2_availability_of_slot_in_block, _4_out);
  and and_6 (and_6_out, block_5_availability_of_slot_in_block, _5_out);
  LED led_7 (.in(block_8_availability_of_slot_in_block));
  Button _6 (.out(_6_out));
  and and_7 (and_7_out, block_8_availability_of_slot_in_block, _6_out);
  BlockChooser Block_Chooser (
    .Button_0(and_1_out), .Button_1(and_4_out), .Button_2(and_3_out), .Button_3(and_2_out),
    .Button_4(and_5_out), .Button_5(and_6_out), .Button_6(and_7_out), .Button_7(or_1_out),
    .Block_Number(Block_Chooser_block_number));
  PathGenerator Path_Generator (.Block_Number(Block_Chooser_block_number), .out_2(Path_Generator_out_2));
  LED led_8 (.in(block_3_out_4));
  Clock clock_1 (.out(clock_1_out));
  LED led_9 (.in(block_1_out_6));
  LED led_10 (.in(block_1_availability_of_slot_in_block));
  LED led_11 (.in(block_1_out_5));
  Block block_1 (
    .Availability_of_Slot_in_Block(block_1_availability_of_slot_in_block), .out_4(block_1_out_4),
    .out_5(block_1_out_5), .out_6(block_1_out_6), .in_1(clock_6_out), .in_2(clock_5_out), .in_3(clock_4_out),
    .Input_for_button7(block_1_input_for_button7));
  LED led_12 (.in(block_1_out_4));
  LED led_13 (.in(block_2_out_6));
  LED led_14 (.in(block_2_availability_of_slot_in_block));
  Block block_2 (
    .Availability_of_Slot_in_Block(block_2_availability_of_slot_in_block), .out_4(block_2_out_4),
    .out_5(block_2_out_5), .out_6(block_2_out_6), .in_1(clock_9_out), .in_2(clock_8_out), .in_3(clock_7_out),
    .Input_for_button7(block_2_input_for_button7));
  LED led_15 (.in(block_2_out_5));
  LED led_16 (.in(block_2_out_4));
  LED led_17 (.in(block_3_availability_of_slot_in_block));
  Block block_3 (
    .Availability_of_Slot_in_Block(block_3_availability_of_slot_in_block), .out_4(block_3_out_4),
    .out_5(block_3_out_5), .out_6(block_3_out_6), .in_1(clock_1_out), .in_2(clock_2_out), .in_3(clock_3_out),
    .Input_for_button7(block_3_input_for_button7));
  LED led_18 (.in(block_3_out_5));
  Clock clock_2 (.out(clock_2_out));
  LED led_19 (.in(block_3_out_6));
  Clock clock_3 (.out(clock_3_out));
  LED led_20 (.in(junction4_1_wl));
  Clock clock_4 (.out(clock_4_out));
  Clock clock_5 (.out(clock_5_out));
  Clock clock_6 (.out(clock_6_out));
  Clock clock_7 (.out(clock_7_out));
  Clock clock_8 (.out(clock_8_out));
  Clock clock_9 (.out(clock_9_out));
  LED led_21 (.in(junction2_1_nl));
  LED led_22 (.in(junction1_1_nl));
  Junction4 junction4_1 (
    .WL(junction4_1_wl), .PathData(junction2_1_newpath4), .Input_Direction(junction2_1_output_direction));  // open: NL, EL, SL
  LED led_23 (.in(block_4_out_4));
  Clock clock_10 (.out(clock_10_out));
  Junction2 junction2_1 (
    .NewPath3(junction2_1_newpath3), .NewPath4(junction2_1_newpath4),
    .Output_Direction(junction2_1_output_direction), .NL(junction2_1_nl), .EL(junction2_1_el),
    .PathData(junction1_1_newpath2), .Input_Direction(junction1_1_output_direction));  // open: WL, SL
  LED led_24 (.in(junction2_1_el));
  Junction1 junction1_1 (
    .PathData(Path_Generator_out_2), .NewPath2(junction1_1_newpath2),
    .Output_Direction(junction1_1_output_direction), .NL(junction1_1_nl));  // open: EL, WL, SL
  Block block_4 (
    .Availability_of_Slot_in_Block(block_4_availability_of_slot_in_block), .out_4(block_4_out_4),
    .out_5(block_4_out_5), .out_6(block_4_out_6), .in_1(clock_10_out), .in_2(clock_11_out),
    .in_3(clock_14_out), .Input_for_button7(block_4_input_for_button7));
  LED led_25 (.in(block_4_availability_of_slot_in_block));
  LED led_26 (.in(block_4_out_5));
  Clock clock_11 (.out(clock_11_out));
  Clock clock_12 (.out(clock_12_out));
  Clock clock_13 (.out(clock_13_out));
  LED led_27 (.in(block_5_out_6));
  LED led_28 (.in(block_5_out_5));
  Block block_5 (
    .Availability_of_Slot_in_Block(block_5_availability_of_slot_in_block), .out_4(block_5_out_4),
    .out_5(block_5_out_5), .out_6(block_5_out_6), .in_1(clock_15_out), .in_2(clock_13_out),
    .in_3(clock_12_out), .Input_for_button7(block_5_input_for_button7));
  LED led_29 (.in(block_5_availability_of_slot_in_block));
  LED led_30 (.in(block_4_out_6));
  Clock clock_14 (.out(clock_14_out));
  Clock clock_15 (.out(clock_15_out));
  LED led_31 (.in(block_5_out_4));
  LED led_32 (.in(junction3_1_sl));
  Junction3 junction3_1 (
    .EL(junction3_1_el), .SL(junction3_1_sl), .PathData(junction2_1_newpath3),
    .Input_Direction(junction2_1_output_direction));  // open: NL, WL
  LED led_33 (.in(junction3_1_el));
  Clock clock_16 (.out(clock_16_out));
  Clock clock_17 (.out(clock_17_out));
  Clock clock_18 (.out(clock_18_out));
  LED led_34 (.in(block_6_availability_of_slot_in_block));
  Block block_6 (
    .Availability_of_Slot_in_Block(block_6_availability_of_slot_in_block), .out_4(block_6_out_4),
    .out_5(block_6_out_5), .out_6(block_6_out_6), .in_1(clock_19_out), .in_2(clock_20_out),
    .in_3(clock_23_out));  // open: Input_for_button7
  LED led_35 (.in(block_6_out_4));
  LED led_36 (.in(block_6_out_5));
  Clock clock_19 (.out(clock_19_out));
  Clock clock_20 (.out(clock_20_out));
  LED led_37 (.in(block_7_availability_of_slot_in_block));
  Block block_7 (
    .Availability_of_Slot_in_Block(block_7_availability_of_slot_in_block), .out_4(block_7_out_4),
    .out_5(block_7_out_5), .out_6(block_7_out_6), .in_1(clock_21_out), .in_2(clock_22_out),
    .in_3(clock_24_out), .Input_for_button7(block_7_input_for_button7));
  LED led_38 (.in(block_7_out_4));
  LED led_39 (.in(block_7_out_5));
  Clock clock_21 (.out(clock_21_out));
  Clock clock_22 (.out(clock_22_out));
  LED led_40 (.in(block_6_out_6));
  Clock clock_23 (.out(clock_23_out));
  LED led_41 (.in(block_7_out_6));
  Clock clock_24 (.out(clock_24_out));
  LED led_42 (.in(block_8_out_4));
  LED led_43 (.in(block_8_out_5));
  LED led_44 (.in(block_8_out_6));
  LED Available ();  // open: in
  Block block_8 (
    .Availability_of_Slot_in_Block(block_8_availability_of_slot_in_block), .out_4(block_8_out_4),
    .out_5(block_8_out_5), .out_6(block_8_out_6), .in_1(clock_16_out), .in_2(clock_17_out),
    .in_3(clock_18_out), .Input_for_button7(block_8_input_for_button7));
  LED led_45 (.in(block_8_availability_of_slot_in_block));
  LED Occupied ();  // open: in
  or or_1 (or_1_out, block_3_input_for_button7, block_1_input_for_button7, block_2_input_for_button7, block_4_input_for_button7, block_7_input_for_button7, block_5_input_for_button7, block_8_input_for_button7);

  // Notes on the sheet:
  //   Insrtuctions:
  //   to identify empty slot
  //   1. Look at the LEDS in each block
  //   2. Press the button for ur desired block
  //   3. The Path to that block will be displayed
  //   Choose which block you want to go to
  //   Block Number
  //   Availability of Block
  //   0
  //   1
  //   4
  //   SCREEN POTRAYING AVAILABLE SLOTS ON LAYOUT AT ENTRANCE
  //   ENTRY
  //   ↑
  //   DIGITAL PARKING
  //   MANAGEMENT SYSTEM
  //   2
  //   5
  //   3
  //   6
  //   BLOCK LAYOUT
  //   Whether slot is available in block
  //   Whether that particular slot is available
  //   The Paking Block with 3 slots
  //   Car Sensors at entrance of block
  //   Which direction you are supposed to enter from
endmodule

module Block (
  input  in_1,
  input  in_2,
  input  in_3,
  output out_4,
  output out_5,
  output out_6,
  output Availability_of_Slot_in_Block,
  output Input_for_button7
);

  Car_Sensor CAR_SENSOR (
    .SENSOR(in_1), .SENSOR_2(in_2), .SENSOR_3(in_3), .Status_of_Parking(out_4), .Status_of_Parking_2(out_5),
    .Status_of_Parking_3(out_6), .Availability_of_Slot(Availability_of_Slot_in_Block));
  or or_1 (Input_for_button7, in_1, in_2, in_3);

  // Notes on the sheet:
  //   LEDS to indicate if slot is empty of full
  //   Clocks at Entrance of Slots
endmodule

module BlockChooser (
  input  Button_0,
  input  Button_1,
  input  Button_2,
  input  Button_3,
  input  Button_4,
  input  Button_5,
  input  Button_6,
  input  Button_7,
  output [2:0] Block_Number
);

  wire d_ff_1_q, d_ff_2_q, d_ff_3_q, d_ff_4_q, d_ff_5_q, d_ff_6_q, d_ff_7_q, d_ff_8_q, or_1_out, undriven,
       undriven_2;

  or or_1 (or_1_out, Button_0, Button_1, Button_2, Button_3, Button_4, Button_5, Button_6, Button_7);
  D_Flip_Flop d_ff_1 (.clk(or_1_out), .D(Button_0), .Q(d_ff_1_q), .preset(undriven));  // open: Qn, en, reset
  D_Flip_Flop d_ff_2 (.clk(or_1_out), .D(Button_1), .Q(d_ff_2_q), .preset(undriven_2));  // open: Qn, en, reset
  D_Flip_Flop d_ff_3 (.clk(or_1_out), .D(Button_2), .Q(d_ff_3_q));  // open: Qn, preset, en, reset
  D_Flip_Flop d_ff_4 (.clk(or_1_out), .D(Button_3), .Q(d_ff_4_q));  // open: Qn, preset, en, reset
  D_Flip_Flop d_ff_5 (.clk(or_1_out), .D(Button_4), .Q(d_ff_5_q));  // open: Qn, preset, en, reset
  D_Flip_Flop d_ff_6 (.clk(or_1_out), .D(Button_5), .Q(d_ff_6_q));  // open: Qn, preset, en, reset
  D_Flip_Flop d_ff_7 (.clk(or_1_out), .D(Button_6), .Q(d_ff_7_q));  // open: Qn, preset, en, reset
  D_Flip_Flop d_ff_8 (.clk(or_1_out), .D(Button_7), .Q(d_ff_8_q));  // open: Qn, preset, en, reset
  Priority_Encoder priority_encoder_1 (
    .in0(d_ff_1_q), .in1(d_ff_2_q), .in2(d_ff_3_q), .in3(d_ff_4_q), .in4(d_ff_5_q), .in5(d_ff_6_q),
    .in6(d_ff_7_q), .in7(d_ff_8_q), .out(Block_Number));  // open: en_in, gs, en_out

  // Notes on the sheet:
  //   Priority
  //   Encoder
endmodule

module PathGenerator (
  input  [2:0] Block_Number,
  output [7:0] out_2
);

  Multiplexer #(.select(3), .width(8), .enable("false")) multiplexer_1 (
    .in0(8'hf8), .in1(8'hf0), .in2(8'hd0), .in3(8'hdc), .in4(8'hc0), .in5(8'hd0), .in6(8'hd4),
    .in7({8{1'b0}}), .out(out_2), .sel(Block_Number));

  // Notes on the sheet:
  //   For Given Parking Layout
  //   Block0: 11111000
  //   Block1: 11110000
  //   Block2: 11010000
  //   Block3: 11011100
  //   Block4: 11000000
  //   Block5: 11010000
  //   Block6: 11010100
  //   Block7: 00000000
  //   note: The binary PathData is represented in hexadecimal for constants
endmodule

module Car_Sensor (
  input  SENSOR,
  input  SENSOR_2,
  input  SENSOR_3,
  output Status_of_Parking,
  output Status_of_Parking_2,
  output Status_of_Parking_3,
  output Availability_of_Slot
);

  wire d_ff_1_q, d_ff_1_qn, d_ff_2_q, d_ff_2_qn, d_ff_3_q, d_ff_3_qn, xor_1_out, xor_2_out, xor_3_out;

  xor xor_1 (xor_1_out, d_ff_1_q, 1'b1);
  xor xor_2 (xor_2_out, d_ff_2_q, 1'b1);
  xor xor_3 (xor_3_out, d_ff_3_q, 1'b1);
  D_Flip_Flop d_ff_1 (.clk(SENSOR), .D(xor_1_out), .Q(d_ff_1_q), .Qn(d_ff_1_qn));  // open: preset, en, reset
  D_Flip_Flop d_ff_2 (.clk(SENSOR_2), .D(xor_2_out), .Q(d_ff_2_q), .Qn(d_ff_2_qn));  // open: preset, en, reset
  D_Flip_Flop d_ff_3 (.clk(SENSOR_3), .D(xor_3_out), .Q(d_ff_3_q), .Qn(d_ff_3_qn));  // open: preset, en, reset
  not not_1 (Status_of_Parking, d_ff_1_qn);
  not not_2 (Status_of_Parking_2, d_ff_2_qn);
  not not_3 (Status_of_Parking_3, d_ff_3_qn);
  nand nand_1 (Availability_of_Slot, Status_of_Parking, Status_of_Parking_2, Status_of_Parking_3);

  // Notes on the sheet:
  //   SLOT1
  //   SLOT2
  //   SLOT3
endmodule

module Junction (
  input  [7:0] Path_Data,
  input  [1:0] Input_Direction,
  output [7:0] New_Path,
  output [1:0] Output_Dir,
  output NL,
  output EL,
  output WL,
  output SL
);

  wire not_1_out, not_2_out, not_3_out, not_4_out, or_1_out;

  not not_1 (not_1_out, Input_Direction[0]);
  not not_2 (not_2_out, Input_Direction[1]);
  or or_1 (or_1_out, Path_Data[6], Path_Data[7]);
  Multiplexer #(.select(2), .enable("false")) multiplexer_1 (
    .in0(not_2_out), .in1(not_1_out), .in2(Input_Direction[0]), .in3(Input_Direction[1]),
    .out(Output_Dir[1]), .sel({Path_Data[6], Path_Data[7]}));
  Multiplexer #(.select(2), .enable("false")) multiplexer_2 (
    .in0(not_1_out), .in1(Input_Direction[1]), .in2(not_2_out), .in3(Input_Direction[0]),
    .out(Output_Dir[0]), .sel({Path_Data[6], Path_Data[7]}));
  not not_3 (not_3_out, Output_Dir[1]);
  not not_4 (not_4_out, Output_Dir[0]);
  and and_1 (NL, not_4_out, or_1_out, not_3_out);
  and and_2 (EL, Output_Dir[0], or_1_out, not_3_out);
  and and_3 (WL, not_4_out, or_1_out, Output_Dir[1]);
  and and_4 (SL, Output_Dir[1], or_1_out, Output_Dir[0]);

  assign New_Path = {Path_Data[5:0], 2'b00};

  // Notes on the sheet:
  //   dir
  //   dis
endmodule

// Junc1
module Junction1 (
  input  [7:0] PathData,
  output [7:0] NewPath2,
  output [1:0] Output_Direction,
  output NL,
  output EL,
  output WL,
  output SL
);

  wire [7:6] junction_1_new_path;

  Junction junction_1 (
    .Path_Data(PathData), .Input_Direction(2'b00), .New_Path({junction_1_new_path, NewPath2[5:0]}),
    .Output_Dir(Output_Direction), .NL(NL), .EL(EL), .WL(WL), .SL(SL));
  and and_1 (NewPath2[6], NL, junction_1_new_path[6]);
  and and_2 (NewPath2[7], junction_1_new_path[7], NL);

  // Notes on the sheet:
  //   Input Direction
endmodule

// Junc2
module Junction2 (
  input  [7:0] PathData,
  input  [1:0] Input_Direction,
  output [7:0] NewPath3,
  output [7:0] NewPath4,
  output [1:0] Output_Direction,
  output NL,
  output EL,
  output WL,
  output SL
);

  wire [7:6] junction_1_new_path;

  Junction junction_1 (
    .Path_Data(PathData), .Input_Direction(Input_Direction), .New_Path({junction_1_new_path, NewPath3[5:0]}),
    .Output_Dir(Output_Direction), .NL(NL), .EL(EL), .WL(WL), .SL(SL));
  and and_1 (NewPath3[6], EL, junction_1_new_path[6]);
  and and_2 (NewPath3[7], junction_1_new_path[7], EL);
  and and_3 (NewPath4[6], NL, junction_1_new_path[6]);
  and and_4 (NewPath4[7], junction_1_new_path[7], NL);

  assign NewPath4[5:0] = NewPath3[5:0];
endmodule

// Junc3
module Junction3 (
  input  [7:0] PathData,
  input  [1:0] Input_Direction,
  output NL,
  output EL,
  output WL,
  output SL
);

  wire [1:0] junction_1_output_dir;
  wire [7:0] junction_1_new_path;

  Junction junction_1 (
    .Path_Data(PathData), .Input_Direction(Input_Direction), .New_Path(junction_1_new_path),
    .Output_Dir(junction_1_output_dir), .NL(NL), .EL(EL), .WL(WL), .SL(SL));
endmodule

// Junc4
module Junction4 (
  input  [7:0] PathData,
  input  [1:0] Input_Direction,
  output NL,
  output EL,
  output WL,
  output SL
);

  wire [1:0] junction_1_output_dir;
  wire [7:0] junction_1_new_path;

  Junction junction_1 (
    .Path_Data(PathData), .Input_Direction(Input_Direction), .New_Path(junction_1_new_path),
    .Output_Dir(junction_1_output_dir), .NL(NL), .EL(EL), .WL(WL), .SL(SL));
endmodule
